# Fritzing sketch Microphone (saved by Fritzing 1.0.1rc)
breadboards: 1

parts:
  Part1 = KY-037 High Sensitivity Sound Detection Module [package="Breakout board"]
  Part2 = Arduino Uno (Rev3)
  R1 = Resistor [tolerance=±5% power=0.25W resistance=220 package=THT]
  R2 = Resistor [tolerance=±5% power=0.25W resistance=220 package=THT]
  LED1 = LED - 5mm [color="Red (633nm)" current=0.030A package="5 mm [THT]"]
  LED2 = LED - 5mm [color="Green (565nm)" current=0.030A package="5 mm [THT]"]

nets:
  N1: Part1.A0, Part2.A0
  N2: Part1.G, Part2.GND, LED1.cathode, LED2.cathode
  N3: Part1.+, Part2.5V
  N4: Part2.D3_PWM, R1.Pin_0
  N5: Part2.D5_PWM, R2.Pin_0
  N6: R1.Pin_1, LED1.anode
  N7: R2.Pin_1, LED2.anode

custom parts:
  KY-037 High Sensitivity Sound Detection Module: KY-037 high sensitivity sound detection module is an analog/digital sensor that uses a condenser microphone to observe changes in environment noise.
